// Logisim project sap2_main.circ as structural Verilog: 1 circuit, main circuit main
module main (
  output [15:0] out_1
);

  register_8 register_8_1 (
    .D1(out_1[0]), .D2(out_1[1]), .D3(out_1[2]), .D4(out_1[3]), .D5(out_1[4]), .D6(out_1[5]), .D7(out_1[6]),
    .D8(out_1[7]), .Q1(out_1[0]), .Q2(out_1[1]), .Q3(out_1[2]), .Q4(out_1[3]), .Q5(out_1[4]), .Q6(out_1[5]),
    .Q7(out_1[6]), .Q8(out_1[7]));  // open: LOAD, CLK, EN, O1, O2, O3, O4, O5, O6, O7, O8
  register_8 register_8_2 (
    .D1(out_1[0]), .D2(out_1[1]), .D3(out_1[2]), .D4(out_1[3]), .D5(out_1[4]), .D6(out_1[5]), .D7(out_1[6]),
    .D8(out_1[7]), .Q1(out_1[0]), .Q2(out_1[1]), .Q3(out_1[2]), .Q4(out_1[3]), .Q5(out_1[4]), .Q6(out_1[5]),
    .Q7(out_1[6]), .Q8(out_1[7]));  // open: LOAD, CLK, EN, O1, O2, O3, O4, O5, O6, O7, O8
  register_8 register_8_3 (
    .D1(out_1[0]), .D2(out_1[1]), .D3(out_1[2]), .D4(out_1[3]), .D5(out_1[4]), .D6(out_1[5]), .D7(out_1[6]),
    .D8(out_1[7]), .Q1(out_1[0]), .Q2(out_1[1]), .Q3(out_1[2]), .Q4(out_1[3]), .Q5(out_1[4]), .Q6(out_1[5]),
    .Q7(out_1[6]), .Q8(out_1[7]));  // open: LOAD, CLK, EN, O1, O2, O3, O4, O5, O6, O7, O8
  register_8 register_8_4 (
    .D1(out_1[0]), .D2(out_1[1]), .D3(out_1[2]), .D4(out_1[3]), .D5(out_1[4]), .D6(out_1[5]), .D7(out_1[6]),
    .D8(out_1[7]), .Q1(out_1[0]), .Q2(out_1[1]), .Q3(out_1[2]), .Q4(out_1[3]), .Q5(out_1[4]), .Q6(out_1[5]),
    .Q7(out_1[6]), .Q8(out_1[7]));  // open: LOAD, CLK, EN, O1, O2, O3, O4, O5, O6, O7, O8

  // Notes on the sheet:
  //   Accumulator Register
  //   Temporary Register
  //   Register B
  //   Register C
endmodule
